// Logisim project alu.circ as structural Verilog: 7 circuits, main circuit alu
module alu (
  input  [31:0] A,
  input  [31:0] B,
  input  [3:0] ALUSel,
  output [31:0] Result
);

  wire comparator_1_lt;
  wire [31:0] add0, and0, mul0, mulh0, mulhu0, or0, sll0, slt0, sra0, srl0, sub0, xor0;

  Shifter #(.width(32)) shifter_1 (.in(A), .\dist (B[4:0]), .out(sll0));
  Comparator #(.width(32)) comparator_1 (.a(A), .b(B), .lt(comparator_1_lt));  // open: gt, eq
  Multiplier #(.mode("twosComplement"), .width(32)) multiplier_1 (.a(A), .b(B), .out(mul0));  // open: cin, cout
  Multiplier #(.width(32)) multiplier_2 (.a(A), .b(B), .cout(mulhu0));  // open: out, cin
  Multiplier #(.mode("twosComplement"), .width(32)) multiplier_3 (.a(A), .b(B), .cout(mulh0));  // open: out, cin
  shifthelper shifthelper_1 (.A(A), .B(B), .signExtend(1'b0), .out_4(srl0));
  assign slt0 = {{31{1'b0}}, comparator_1_lt};  // Bit_Extender bit_extender_1
  shifthelper shifthelper_2 (.A(A), .B(B), .signExtend(1'b1), .out_4(sra0));
  Multiplexer #(.enable("false"), .select(4), .width(32)) multiplexer_1 (
    .in0(add0), .in1(and0), .in2(or0), .in3(xor0), .in4(srl0), .in5(sra0), .in6(sll0), .in7(slt0),
    .in10(mul0), .in11(mulhu0), .in12(sub0), .in13(B), .in14(mulh0), .out(Result), .sel(ALUSel));  // open: in8, in9, in15
  Adder #(.width(32)) adder_1 (.a(A), .b(B), .out(add0));  // open: cin, cout
  assign and0 = A & B;  // AND_Gate and_1, 32 bits wide
  assign or0 = A | B;  // OR_Gate or_1, 32 bits wide
  assign xor0 = A ^ B;  // XOR_Gate xor_1, 32 bits wide
  Subtractor #(.width(32)) subtractor_1 (.a(A), .b(B), .out(sub0));  // open: bin, bout

  // Other names for the same wires on the sheet: bsel0[31:0] = B

  // Notes on the sheet:
  //   INPUTS to your circuit
  //   DON'T CHANGE THE LOCATIONS OF THE INPUTS AND OUTPUTS!
  //   OUTPUT from your circuit
endmodule

module shift1 (
  input  [31:0] in_1,
  input  in_2,
  output [31:0] out_3
);

  and and_1 (out_3[31], in_1[31], in_2);

  assign out_3[30:0] = in_1[31:1];
endmodule

module shift2 (
  input  [31:0] in_1,
  input  in_2,
  output [31:0] out_3
);

  wire [31:0] shift1_1_out_3;

  shift1 shift1_1 (.in_1(in_1), .in_2(in_2), .out_3(shift1_1_out_3));
  shift1 shift1_2 (.in_1(shift1_1_out_3), .in_2(in_2), .out_3(out_3));
endmodule

module shift4 (
  input  [31:0] in_1,
  input  in_2,
  output [31:0] out_3
);

  wire [31:0] shift2_1_out_3;

  shift2 shift2_1 (.in_1(in_1), .in_2(in_2), .out_3(shift2_1_out_3));
  shift2 shift2_2 (.in_1(shift2_1_out_3), .in_2(in_2), .out_3(out_3));
endmodule

module shift8 (
  input  [31:0] in_1,
  input  in_2,
  output [31:0] out_3
);

  wire [31:0] shift4_1_out_3;

  shift4 shift4_1 (.in_1(in_1), .in_2(in_2), .out_3(shift4_1_out_3));
  shift4 shift4_2 (.in_1(shift4_1_out_3), .in_2(in_2), .out_3(out_3));
endmodule

module shift16 (
  input  [31:0] in_1,
  input  in_2,
  output [31:0] out_3
);

  wire [31:0] shift8_1_out_3;

  shift8 shift8_1 (.in_1(in_1), .in_2(in_2), .out_3(shift8_1_out_3));
  shift8 shift8_2 (.in_1(shift8_1_out_3), .in_2(in_2), .out_3(out_3));
endmodule

module shifthelper (
  input  [31:0] A,
  input  [31:0] B,
  input  signExtend,
  output [31:0] out_4
);

  wire [31:0] multiplexer_2_out, multiplexer_3_out, multiplexer_4_out, multiplexer_5_out, shift1_1_out_3,
       shift2_1_out_3, shift4_1_out_3, shift8_1_out_3, shift16_1_out_3;

  Multiplexer #(.enable("false"), .width(32)) multiplexer_1 (
    .in0(multiplexer_5_out), .in1(shift1_1_out_3), .out(out_4), .sel(B[0]));
  Multiplexer #(.enable("false"), .width(32)) multiplexer_2 (
    .in0(A), .in1(shift16_1_out_3), .out(multiplexer_2_out), .sel(B[4]));
  Multiplexer #(.enable("false"), .width(32)) multiplexer_3 (
    .in0(multiplexer_4_out), .in1(shift4_1_out_3), .out(multiplexer_3_out), .sel(B[2]));
  Multiplexer #(.enable("false"), .width(32)) multiplexer_4 (
    .in0(multiplexer_2_out), .in1(shift8_1_out_3), .out(multiplexer_4_out), .sel(B[3]));
  shift16 shift16_1 (.in_1(A), .in_2(signExtend), .out_3(shift16_1_out_3));
  shift1 shift1_1 (.in_1(multiplexer_5_out), .in_2(signExtend), .out_3(shift1_1_out_3));
  Multiplexer #(.enable("false"), .width(32)) multiplexer_5 (
    .in0(multiplexer_3_out), .in1(shift2_1_out_3), .out(multiplexer_5_out), .sel(B[1]));
  shift4 shift4_1 (.in_1(multiplexer_4_out), .in_2(signExtend), .out_3(shift4_1_out_3));
  shift8 shift8_1 (.in_1(multiplexer_2_out), .in_2(signExtend), .out_3(shift8_1_out_3));
  shift2 shift2_1 (.in_1(multiplexer_3_out), .in_2(signExtend), .out_3(shift2_1_out_3));
endmodule
