// Logisim project control_logic.circ as structural Verilog: 1 circuit, main circuit control_logic
module control_logic (
  input  [31:0] inst,
  input  BrEq,
  input  BrLt,
  output PCSel,
  output RegWEn,
  output [2:0] ImmSel,
  output BrUn,
  output ASel,
  output BSel,
  output [3:0] ALUSel,
  output [3:0] MemRW,
  output [1:0] WBSel,
  output CSRSel,
  output CSRWen
);

  wire and_2_out, and_3_out, and_4_out, and_5_out, and_7_out, and_8_out, and_9_out, b_type, func3_0, func3_1,
       func3_2, func3_4, func3_5, func3_6, func3_7, func7_val0, func7_val1, func7_val20, i_type, i_type_jalr,
       i_type_loads, imm_val0, imm_val20, j_type_jal, multiplexer_8_out, multiplexer_9_out,
       multiplexer_10_out, multiplexer_11_out, not_1_out, not_2_out, or_1_out, or_2_out, or_3_out, or_4_out,
       or_5_out, or_6_out, or_7_out, or_8_out, or_9_out, or_10_out, or_11_out, or_12_out, or_13_out,
       or_14_out, r_type, s_type, u_type_auipc, u_type_lui;
  wire [1:0] multiplexer_32_out;
  wire [2:0] multiplexer_14_out, multiplexer_18_out, multiplexer_19_out, multiplexer_20_out;
  wire [3:0] multiplexer_2_out, multiplexer_3_out, multiplexer_4_out, multiplexer_5_out, multiplexer_6_out,
       multiplexer_13_out, multiplexer_15_out, multiplexer_16_out, multiplexer_21_out, multiplexer_22_out,
       multiplexer_23_out, multiplexer_25_out, multiplexer_26_out, multiplexer_27_out, multiplexer_28_out,
       multiplexer_29_out, multiplexer_33_out, multiplexer_34_out, multiplexer_35_out, multiplexer_37_out,
       multiplexer_38_out;

  Comparator #(.mode("unsigned"), .width(3)) comparator_1 (.a(inst[14:12]), .b(3'b001), .eq(func3_1));  // open: gt, lt
  Comparator #(.mode("unsigned"), .width(3)) comparator_2 (.a(inst[14:12]), .b(3'b000), .eq(func3_0));  // open: gt, lt
  Comparator #(.mode("unsigned"), .width(3)) comparator_3 (.a(inst[14:12]), .b(3'b100), .eq(func3_4));  // open: gt, lt
  Comparator #(.mode("unsigned"), .width(3)) comparator_4 (.a(inst[14:12]), .b(3'b101), .eq(func3_5));  // open: gt, lt
  Comparator #(.mode("unsigned"), .width(3)) comparator_5 (.a(inst[14:12]), .b(3'b010), .eq(func3_2));  // open: gt, lt
  Comparator #(.width(7)) comparator_6 (.a(inst[31:25]), .b({7{1'b0}}), .eq(imm_val0));  // open: gt, lt
  Comparator #(.width(7)) comparator_7 (.a(inst[31:25]), .b(7'b0100000), .eq(imm_val20));  // open: gt, lt
  Comparator #(.width(7)) comparator_8 (.a(inst[31:25]), .b({7{1'b0}}), .eq(func7_val0));  // open: gt, lt
  Comparator #(.width(7)) comparator_9 (.a(inst[31:25]), .b(7'b0000001), .eq(func7_val1));  // open: gt, lt
  Comparator #(.width(7)) comparator_10 (.a(inst[31:25]), .b(7'b0100000), .eq(func7_val20));  // open: gt, lt
  Multiplexer #(.enable("false")) multiplexer_1 (.in0(1'b1), .in1(1'b0), .out(RegWEn), .sel(or_1_out));
  or or_1 (or_1_out, s_type, b_type);
  Comparator #(.mode("unsigned"), .width(7)) comparator_11 (
    .a(inst[6:0]), .b(7'b0110011), .eq(r_type));  // open: gt, lt
  Comparator #(.mode("unsigned"), .width(7)) comparator_12 (
    .a(inst[6:0]), .b(7'b0000011), .eq(i_type_loads));  // open: gt, lt
  Comparator #(.mode("unsigned"), .width(7)) comparator_13 (
    .a(inst[6:0]), .b(7'b0010011), .eq(i_type));  // open: gt, lt
  Comparator #(.mode("unsigned"), .width(7)) comparator_14 (
    .a(inst[6:0]), .b(7'b0100011), .eq(s_type));  // open: gt, lt
  Comparator #(.mode("unsigned"), .width(7)) comparator_15 (
    .a(inst[6:0]), .b(7'b1100011), .eq(b_type));  // open: gt, lt
  Comparator #(.mode("unsigned"), .width(7)) comparator_16 (
    .a(inst[6:0]), .b(7'b0010111), .eq(u_type_auipc));  // open: gt, lt
  Comparator #(.mode("unsigned"), .width(7)) comparator_17 (
    .a(inst[6:0]), .b(7'b0110111), .eq(u_type_lui));  // open: gt, lt
  Comparator #(.mode("unsigned"), .width(7)) comparator_18 (
    .a(inst[6:0]), .b(7'b1101111), .eq(j_type_jal));  // open: gt, lt
  Comparator #(.mode("unsigned"), .width(7)) comparator_19 (
    .a(inst[6:0]), .b(7'b1100111), .eq(i_type_jalr));  // open: gt, lt
  Comparator #(.mode("unsigned"), .width(7)) comparator_20 (
    .a(inst[6:0]), .b(7'b1110011), .eq(CSRWen));  // open: gt, lt
  Comparator #(.mode("unsigned"), .width(3)) comparator_21 (.a(inst[14:12]), .b(3'b110), .eq(func3_6));  // open: gt, lt
  Multiplexer #(.enable("false"), .width(4)) multiplexer_2 (
    .in0(4'b0000), .in1(4'b1101), .out(multiplexer_2_out), .sel(u_type_lui));
  or or_2 (or_2_out, func3_5, func3_7);
  Comparator #(.mode("unsigned"), .width(3)) comparator_22 (.a(inst[14:12]), .b(3'b111), .eq(func3_7));  // open: gt, lt
  Multiplexer #(.enable("false"), .width(4)) multiplexer_3 (
    .in0(4'b0000), .in1(4'b0110), .out(multiplexer_3_out), .sel(imm_val0));
  or or_3 (or_3_out, func3_4, func3_6);
  not not_1 (not_1_out, BrLt);
  and and_1 (CSRSel, CSRWen, func3_5);
  Multiplexer #(.enable("false"), .select(3), .width(4)) multiplexer_4 (
    .in0(4'b0000), .in1(multiplexer_3_out), .in2(4'b0111), .in4(4'b0011), .in5(multiplexer_5_out),
    .in6(4'b0010), .in7(4'b0001), .out(multiplexer_4_out), .sel(inst[14:12]));  // open: in3
  Multiplexer #(.enable("false"), .width(4)) multiplexer_5 (
    .in0(4'b0000), .in1(multiplexer_6_out), .out(multiplexer_5_out), .sel(or_4_out));
  or or_4 (or_4_out, imm_val0, imm_val20);
  Multiplexer #(.enable("false"), .width(4)) multiplexer_6 (
    .in0(4'b0101), .in1(4'b0100), .out(multiplexer_6_out), .sel(imm_val0));
  not not_2 (not_2_out, BrEq);
  and and_2 (and_2_out, b_type, or_2_out, not_1_out);
  or or_5 (or_5_out, j_type_jal, i_type_jalr);
  or or_6 (or_6_out, r_type, i_type);
  Multiplexer #(.enable("false")) multiplexer_7 (.in0(multiplexer_8_out), .in1(1'b1), .out(PCSel), .sel(and_3_out));
  and and_3 (and_3_out, b_type, func3_0, BrEq);
  Multiplexer #(.enable("false")) multiplexer_8 (
    .in0(multiplexer_9_out), .in1(1'b1), .out(multiplexer_8_out), .sel(and_4_out));
  and and_4 (and_4_out, b_type, func3_1, not_2_out);
  Multiplexer #(.enable("false")) multiplexer_9 (
    .in0(multiplexer_10_out), .in1(1'b1), .out(multiplexer_9_out), .sel(and_5_out));
  and and_5 (and_5_out, b_type, or_3_out, BrLt);
  Multiplexer #(.enable("false")) multiplexer_10 (
    .in0(multiplexer_11_out), .in1(1'b1), .out(multiplexer_10_out), .sel(and_2_out));
  Multiplexer #(.enable("false")) multiplexer_11 (.in0(1'b0), .in1(1'b1), .out(multiplexer_11_out), .sel(or_5_out));
  or or_7 (or_7_out, func3_6, func3_7);
  Multiplexer #(.enable("false"), .width(4)) multiplexer_12 (
    .in0(multiplexer_2_out), .in1(multiplexer_13_out), .out(ALUSel), .sel(or_6_out));
  Multiplexer #(.enable("false"), .width(4)) multiplexer_13 (
    .in0(multiplexer_4_out), .in1(multiplexer_33_out), .out(multiplexer_13_out), .sel(r_type));
  or or_8 (or_8_out, i_type_loads, i_type_jalr, CSRWen, i_type);
  Multiplexer #(.enable("false"), .width(3)) multiplexer_14 (
    .in0(3'b100), .in1(3'b101), .out(multiplexer_14_out), .sel(j_type_jal));
  and and_6 (BrUn, b_type, or_7_out);
  or or_9 (or_9_out, func7_val0, func7_val1, func7_val20);
  Multiplexer #(.enable("false"), .width(4)) multiplexer_15 (
    .in0(4'b0000), .in1(multiplexer_16_out), .out(multiplexer_15_out), .sel(or_10_out));
  or or_10 (or_10_out, func7_val1, func7_val20);
  Multiplexer #(.enable("false"), .width(4)) multiplexer_16 (
    .in0(4'b1010), .in1(4'b1100), .out(multiplexer_16_out), .sel(func7_val20));
  or or_11 (or_11_out, func7_val1, func7_val0);
  Multiplexer #(.enable("false"), .width(3)) multiplexer_17 (
    .in0(multiplexer_18_out), .in1(3'b001), .out(ImmSel), .sel(or_8_out));
  Multiplexer #(.enable("false"), .width(3)) multiplexer_18 (
    .in0(multiplexer_19_out), .in1(3'b000), .out(multiplexer_18_out), .sel(r_type));
  Multiplexer #(.enable("false"), .width(3)) multiplexer_19 (
    .in0(multiplexer_20_out), .in1(3'b010), .out(multiplexer_19_out), .sel(s_type));
  Multiplexer #(.enable("false"), .width(3)) multiplexer_20 (
    .in0(multiplexer_14_out), .in1(3'b011), .out(multiplexer_20_out), .sel(b_type));
  Multiplexer #(.enable("false"), .width(4)) multiplexer_21 (
    .in0(4'b0000), .in1(multiplexer_15_out), .out(multiplexer_21_out), .sel(or_9_out));
  Multiplexer #(.enable("false"), .width(4)) multiplexer_22 (
    .in0(4'b0000), .in1(multiplexer_23_out), .out(multiplexer_22_out), .sel(or_11_out));
  Multiplexer #(.enable("false"), .width(4)) multiplexer_23 (
    .in0(4'b0110), .in1(4'b1110), .out(multiplexer_23_out), .sel(func7_val1));
  and and_7 (and_7_out, s_type, func3_0);
  and and_8 (and_8_out, s_type, func3_1);
  and and_9 (and_9_out, s_type, func3_2);
  Multiplexer #(.enable("false"), .width(4)) multiplexer_24 (
    .in0(multiplexer_25_out), .in1(4'b0001), .out(MemRW), .sel(and_7_out));
  Multiplexer #(.enable("false"), .width(4)) multiplexer_25 (
    .in0(multiplexer_26_out), .in1(4'b0011), .out(multiplexer_25_out), .sel(and_8_out));
  Multiplexer #(.enable("false"), .width(4)) multiplexer_26 (
    .in0(4'b0000), .in1(4'b1111), .out(multiplexer_26_out), .sel(and_9_out));
  Multiplexer #(.enable("false"), .width(4)) multiplexer_27 (
    .in0(4'b0000), .in1(4'b0111), .out(multiplexer_27_out), .sel(func7_val0));
  Multiplexer #(.enable("false"), .width(4)) multiplexer_28 (
    .in0(4'b0000), .in1(4'b1011), .out(multiplexer_28_out), .sel(func7_val1));
  Multiplexer #(.enable("false"), .width(4)) multiplexer_29 (
    .in0(4'b0000), .in1(4'b0011), .out(multiplexer_29_out), .sel(func7_val0));
  or or_12 (or_12_out, i_type_loads, j_type_jal, i_type_jalr);
  or or_13 (or_13_out, func7_val0, func7_val20);
  Multiplexer #(.enable("false")) multiplexer_30 (.in0(1'b1), .in1(1'b0), .out(BSel), .sel(r_type));
  or or_14 (or_14_out, j_type_jal, u_type_auipc, b_type);
  Multiplexer #(.enable("false"), .width(2)) multiplexer_31 (
    .in0(2'b01), .in1(multiplexer_32_out), .out(WBSel), .sel(or_12_out));
  Multiplexer #(.enable("false"), .width(2)) multiplexer_32 (
    .in0(2'b00), .in1(2'b10), .out(multiplexer_32_out), .sel(i_type_loads));
  Multiplexer #(.enable("false"), .select(3), .width(4)) multiplexer_33 (
    .in0(multiplexer_21_out), .in1(multiplexer_22_out), .in2(multiplexer_27_out), .in3(multiplexer_28_out),
    .in4(multiplexer_29_out), .in5(multiplexer_34_out), .in6(multiplexer_37_out), .in7(multiplexer_38_out),
    .out(multiplexer_33_out), .sel(inst[14:12]));
  Multiplexer #(.enable("false"), .width(4)) multiplexer_34 (
    .in0(4'b0000), .in1(multiplexer_35_out), .out(multiplexer_34_out), .sel(or_13_out));
  Multiplexer #(.enable("false"), .width(4)) multiplexer_35 (
    .in0(4'b0100), .in1(4'b0101), .out(multiplexer_35_out), .sel(func7_val20));
  Multiplexer #(.enable("false")) multiplexer_36 (.in0(1'b0), .in1(1'b1), .out(ASel), .sel(or_14_out));
  Multiplexer #(.enable("false"), .width(4)) multiplexer_37 (
    .in0(4'b0000), .in1(4'b0010), .out(multiplexer_37_out), .sel(func7_val0));
  Multiplexer #(.enable("false"), .width(4)) multiplexer_38 (
    .in0(4'b0000), .in1(4'b0001), .out(multiplexer_38_out), .sel(func7_val0));

  // Other names for the same wires on the sheet: i_type_csrw = CSRWen; opcode[6:0] = inst[6:0];
  //   func3[2:0] = inst[14:12]; i_imm_val[11:0] = inst[31:20]; func7[6:0] = inst[31:25]

  // Notes on the sheet:
  //   INPUTS to your circuit
  //   DON'T CHANGE THE LOCATIONS OF THE INPUTS AND OUTPUTS!
  //   OUTPUT from your circuit
  //   CSRSel -> 1 for immediate, 0 for rs1
endmodule
