// Logisim project cpu.circ as structural Verilog: 1 circuit, main circuit cpu
module cpu (
  input  clk,
  input  [31:0] INSTRUCTION,
  input  [31:0] READ_DATA,
  output [31:0] WRITE_ADDRESS,
  output [31:0] PROGRAM_COUNTER,
  output [31:0] ra,
  output [31:0] sp,
  output [31:0] t0,
  output [31:0] t1,
  output [31:0] t2,
  output [31:0] s0,
  output [31:0] s1,
  output [31:0] a0,
  output [31:0] tohost,
  output [3:0] WRITE_ENABLE,
  output [31:0] WRITE_DATA
);

  wire ASel, BrEq, BrLt, BrUn, BSel, CSRSel, CSRWen, func3_0, func3_1, PCSel, RegWen;
  wire [1:0] WBSel;
  wire [2:0] func3, immsel;
  wire [3:0] ALUSel, MemRW;
  wire [4:0] bit_extender_2_out, bit_extender_3_out, csrImm, multiplier_1_out, multiplier_2_out;
  wire [11:0] csrAddress, instr2;
  wire [31:0] adder_2_out, bit_extender_1_out, bit_extender_4_out, bit_extender_5_out, CSR_in, imm,
       multiplexer_1_out, multiplexer_2_out, multiplexer_4_out, multiplexer_5_out, multiplexer_8_out,
       newREAD_DATA, newREAD_DATA0, PC_2, PC_4, Read_Data1, Read_Data2, Write_Data_t;

  Adder #(.width(32)) adder_1 (.a(PROGRAM_COUNTER), .b(32'h4), .out(PC_4));  // open: cin, cout
  Multiplexer #(.enable("false"), .width(32)) multiplexer_1 (
    .in0(PC_4), .in1(WRITE_ADDRESS), .out(multiplexer_1_out), .sel(PCSel));
  Register #(.width(32)) PC (.D(multiplexer_1_out), .en(1'b1), .clk(clk), .Q(PROGRAM_COUNTER));  // open: clr
  Multiplexer #(.enable("false"), .width(32)) multiplexer_2 (
    .in0(INSTRUCTION), .in1(32'h13), .out(multiplexer_2_out), .sel(PCSel));
  Register #(.width(32)) register_1 (.D(PROGRAM_COUNTER), .clk(clk), .Q(PC_2));  // open: en, clr
  Register #(.width(32)) register_2 (
    .D(multiplexer_2_out), .clk(clk), .Q({csrAddress, csrImm, func3, instr2}));  // open: en, clr
  control_logic control_logic_1 (
    .CSRWen(CSRWen), .PCSel(PCSel), .RegWEn(RegWen), .ImmSel(immsel), .BrUn(BrUn), .ASel(ASel), .BSel(BSel),
    .ALUSel(ALUSel), .MemRW(MemRW), .WBSel(WBSel), .CSRSel(CSRSel),
    .inst({csrAddress, csrImm, func3, instr2}), .BrEq(BrEq), .BrLt(BrLt));
  imm_gen imm_gen_1 (.inst({csrAddress, csrImm, func3, instr2}), .ImmSel(immsel), .imm(imm));
  regfile regfile_1 (
    .rs1(csrImm), .rs2(csrAddress[4:0]), .rd(instr2[11:7]), .Write_Data(Write_Data_t), .RegWEn(RegWen),
    .clk(clk), .ra(ra), .sp(sp), .t0(t0), .t1(t1), .t2(t2), .s0(s0), .s1(s1), .a0(a0),
    .Read_Data_1(Read_Data1), .Read_Data_2(Read_Data2));
  branch_comp branch_comp_1 (.rs1(Read_Data1), .rs2(Read_Data2), .BrUn(BrUn), .BrEq(BrEq), .BrLt(BrLt));
  Multiplexer #(.enable("false"), .width(32)) multiplexer_3 (
    .in0(Read_Data1), .in1(bit_extender_1_out), .out(CSR_in), .sel(CSRSel));
  assign bit_extender_1_out = {{27{1'b0}}, csrImm};  // Bit_Extender bit_extender_1
  Multiplexer #(.enable("false"), .width(32)) multiplexer_4 (
    .in0(Read_Data1), .in1(PC_2), .out(multiplexer_4_out), .sel(ASel));
  Multiplexer #(.enable("false"), .width(32)) multiplexer_5 (
    .in0(Read_Data2), .in1(imm), .out(multiplexer_5_out), .sel(BSel));
  alu alu_1 (.Result(WRITE_ADDRESS), .A(multiplexer_4_out), .B(multiplexer_5_out), .ALUSel(ALUSel));
  csr csr_1 (.CSR_address(csrAddress), .CSR_din(CSR_in), .CSR_WE(CSRWen), .clk(clk), .tohost(tohost));
  assign bit_extender_2_out = {{3{1'b0}}, WRITE_ADDRESS[1:0]};  // Bit_Extender bit_extender_2
  Adder #(.width(32)) adder_2 (.a(PC_2), .b(32'h4), .out(adder_2_out));  // open: cin, cout
  Shifter #(.width(4)) shifter_1 (.in(MemRW), .\dist (WRITE_ADDRESS[1:0]), .out(WRITE_ENABLE));
  Multiplier #(.mode("twosComplement"), .width(5)) multiplier_1 (
    .a(bit_extender_2_out), .b(5'b01000), .out(multiplier_1_out));  // open: cin, cout
  Comparator #(.width(3)) comparator_1 (.a(func3), .b(3'b000), .eq(func3_0));  // open: gt, lt
  Comparator #(.width(3)) comparator_2 (.a(func3), .b(3'b001), .eq(func3_1));  // open: gt, lt
  Multiplexer #(.enable("false"), .select(2), .width(32)) multiplexer_6 (
    .in0(adder_2_out), .in1(WRITE_ADDRESS), .in2(newREAD_DATA), .out(Write_Data_t), .sel(WBSel));  // open: in3
  Shifter #(.shift("lr"), .width(32)) shifter_2 (.in(READ_DATA), .\dist (multiplier_1_out), .out(newREAD_DATA0));
  assign bit_extender_3_out = {{3{1'b0}}, WRITE_ADDRESS[1:0]};  // Bit_Extender bit_extender_3
  Multiplier #(.mode("twosComplement"), .width(5)) multiplier_2 (
    .a(bit_extender_3_out), .b(5'b01000), .out(multiplier_2_out));  // open: cin, cout
  Multiplexer #(.enable("false"), .width(32)) multiplexer_7 (
    .in0(multiplexer_8_out), .in1(bit_extender_5_out), .out(newREAD_DATA), .sel(func3_0));
  Multiplexer #(.enable("false"), .width(32)) multiplexer_8 (
    .in0(newREAD_DATA0), .in1(bit_extender_4_out), .out(multiplexer_8_out), .sel(func3_1));
  Shifter #(.width(32)) shifter_3 (.in(Read_Data2), .\dist (multiplier_2_out), .out(WRITE_DATA));
  assign bit_extender_4_out = {{16{newREAD_DATA0[15]}}, newREAD_DATA0[15:0]};  // Bit_Extender bit_extender_4
  assign bit_extender_5_out = {{24{newREAD_DATA0[7]}}, newREAD_DATA0[7:0]};  // Bit_Extender bit_extender_5

  // Other names for the same wires on the sheet: address_bit2[1:0] = WRITE_ADDRESS[1:0]; ALUres[31:0] = WRITE_ADDRESS;
  //   opcode[6:0] = instr2[6:0]; rd[4:0] = instr2[11:7]; instr2[31:12] = {csrAddress, csrImm, func3};
  //   rs1[4:0] = csrImm; rs2[4:0] = csrAddress[4:0]

  // Notes on the sheet:
  //   Output to IMEM
  //   IMEM (do **NOT** move this)
  //   Inputs from IMEM
  //   It is OK to move the PC, RegFile, ALU, MEM, Branch Comp, Imm Gen, and Control Logic to wherever is most convenient for you when constructing your CPU, and to delete this text
  //   Inputs/Outputs for testing. Do **NOT** move these.
  //   Outputs To DMEM
  //   DMEM (do **NOT** move this)
  //   Inputs From DMEM
endmodule
