// Logisim project csr.circ as structural Verilog: 1 circuit, main circuit csr
module csr (
  input  [11:0] CSR_address,
  input  [31:0] CSR_din,
  input  CSR_WE,
  input  clk,
  output [31:0] tohost
);

  wire comparator_1_eq, WE_new;

  Comparator #(.width(12)) comparator_1 (.a(CSR_address), .b(12'h51e), .eq(comparator_1_eq));  // open: gt, lt
  Multiplexer #(.enable("false")) multiplexer_1 (.in0(1'b0), .in1(CSR_WE), .out(WE_new), .sel(comparator_1_eq));
  Register #(.width(32)) register_1 (.D(CSR_din), .en(WE_new), .clk(clk), .Q(tohost));  // open: clr

  // Other names for the same wires on the sheet: address[11:0] = CSR_address; data[31:0] = CSR_din; WE = CSR_WE

  // Notes on the sheet:
  //   INPUTS to your circuit
  //   if address isn't 0x051e, write enable = 0
  //   DON'T CHANGE THE LOCATIONS OF THE INPUTS AND OUTPUTS!
  //   OUTPUT from your circuit
endmodule
