// Logisim project regfile.circ as structural Verilog: 1 circuit, main circuit regfile
module regfile (
  input  [4:0] rs1,
  input  [4:0] rs2,
  input  [4:0] rd,
  input  [31:0] Write_Data,
  input  RegWEn,
  input  clk,
  output [31:0] ra,
  output [31:0] sp,
  output [31:0] t0,
  output [31:0] t1,
  output [31:0] t2,
  output [31:0] s0,
  output [31:0] s1,
  output [31:0] a0,
  output [31:0] Read_Data_1,
  output [31:0] Read_Data_2
);

  wire a0_in, ra_in, s0_in, s1_in, sp_in, t0_in, t1_in, t2_in, x3_in, x4_in, x11_in, x12_in, x13_in, x14_in,
       x15_in, x16_in, x17_in, x18_in, x19_in, x20_in, x21_in, x22_in, x23_in, x24_in, x25_in, x26_in,
       x27_in, x28_in, x29_in, x30_in, x31_in;
  wire [31:0] undriven, x3, x4, x11, x12, x13, x14, x15, x16, x17, x18, x19, x20, x21, x22, x23, x24, x25,
       x26, x27, x28, x29, x30, x31;

  Multiplexer #(.enable("false"), .select(5), .width(32)) multiplexer_1 (
    .in0({32{1'b0}}), .in1(ra), .in2(sp), .in3(x3), .in4(x4), .in5(t0), .in6(t1), .in7(t2), .in8(s0),
    .in9(s1), .in10(a0), .in11(x11), .in12(x12), .in13(x13), .in14(x14), .in15(x15), .in16(x16), .in17(x17),
    .in18(x18), .in19(x19), .in20(x20), .in21(x21), .in22(x22), .in23(x23), .in24(x24), .in25(x25),
    .in26(x26), .in27(x27), .in28(x28), .in29(x29), .in30(x30), .in31(x31), .out(Read_Data_1), .sel(rs1));
  Register #(.width(32)) register_1 (.D(Write_Data), .en(x3_in), .clk(clk), .Q(x3));  // open: clr
  Register #(.width(32)) register_2 (.D(Write_Data), .en(x4_in), .clk(clk), .Q(x4));  // open: clr
  Register #(.width(32)) register_3 (.D(Write_Data), .en(x11_in), .clk(clk), .Q(x11));  // open: clr
  Register #(.width(32)) register_4 (.D(Write_Data), .en(x12_in), .clk(clk), .Q(x12));  // open: clr
  Register #(.width(32)) register_5 (.D(Write_Data), .en(x13_in), .clk(clk), .Q(x13));  // open: clr
  Register #(.width(32)) register_6 (.D(Write_Data), .en(x14_in), .clk(clk), .Q(x14));  // open: clr
  Register #(.width(32)) register_7 (.D(Write_Data), .en(x16_in), .clk(clk), .Q(x16));  // open: clr
  Register #(.width(32)) register_8 (.D(Write_Data), .clk(clk), .Q(x19));  // open: en, clr
  Register #(.width(32)) register_9 (.D(Write_Data), .en(x20_in), .clk(clk), .Q(x20));  // open: clr
  Register #(.width(32)) register_10 (.D(Write_Data), .en(x21_in), .clk(clk), .Q(x21));  // open: clr
  Register #(.width(32)) register_11 (.D(Write_Data), .en(x22_in), .clk(clk), .Q(x22));  // open: clr
  Register #(.width(32)) register_12 (.D(Write_Data), .en(x23_in), .clk(clk), .Q(x23));  // open: clr
  Register #(.width(32)) register_13 (.D(Write_Data), .en(x18_in), .clk(clk), .Q(x18));  // open: clr
  Register #(.width(32)) register_14 (.D(Write_Data), .en(x24_in), .clk(clk), .Q(x24));  // open: clr
  Register #(.width(32)) register_15 (.D(Write_Data), .en(x25_in), .clk(clk), .Q(x25));  // open: clr
  Register #(.width(32)) register_16 (.D(Write_Data), .en(x26_in), .clk(clk), .Q(x26));  // open: clr
  Register #(.width(32)) register_17 (.D(Write_Data), .en(x27_in), .clk(clk), .Q(x27));  // open: clr
  Register #(.width(32)) register_18 (.D(Write_Data), .en(x28_in), .clk(clk), .Q(x28));  // open: clr
  Multiplexer #(.enable("false"), .select(5), .width(32)) multiplexer_2 (
    .in0({32{1'b0}}), .in1(ra), .in2(sp), .in3(x3), .in4(x4), .in5(t0), .in6(t1), .in7(t2), .in8(s0),
    .in9(s1), .in10(a0), .in11(x11), .in12(x12), .in13(x13), .in14(x14), .in15(x15), .in16(x16), .in17(x17),
    .in18(x18), .in19(x19), .in20(x20), .in21(x21), .in22(x22), .in23(x23), .in24(x24), .in25(x25),
    .in26(x26), .in27(x27), .in28(x28), .in29(x29), .in30(x30), .in31(undriven), .out(Read_Data_2), .sel(rs2));
  Register #(.width(32)) register_19 (.D(Write_Data), .en(x15_in), .clk(clk), .Q(x15));  // open: clr
  Register #(.width(32)) register_20 (.D(Write_Data), .en(x29_in), .clk(clk), .Q(x29));  // open: clr
  Register #(.width(32)) register_21 (.D(Write_Data), .en(x30_in), .clk(clk), .Q(x30));  // open: clr
  Register #(.width(32)) register_22 (.D(Write_Data), .en(x31_in), .clk(clk), .Q(x31));  // open: clr
  Register #(.width(32)) register_23 (.D(Write_Data), .en(ra_in), .clk(clk), .Q(ra));  // open: clr
  Register #(.width(32)) register_24 (.D(Write_Data), .en(sp_in), .clk(clk), .Q(sp));  // open: clr
  Register #(.width(32)) register_25 (.D(Write_Data), .en(t0_in), .clk(clk), .Q(t0));  // open: clr
  Register #(.width(32)) register_26 (.D(Write_Data), .en(t1_in), .clk(clk), .Q(t1));  // open: clr
  Register #(.width(32)) register_27 (.D(Write_Data), .en(t2_in), .clk(clk), .Q(t2));  // open: clr
  Register #(.width(32)) register_28 (.D(Write_Data), .en(s0_in), .clk(clk), .Q(s0));  // open: clr
  Register #(.width(32)) register_29 (.D(Write_Data), .en(a0_in), .clk(clk), .Q(a0));  // open: clr
  Register #(.width(32)) register_30 (.D(Write_Data), .en(s1_in), .clk(clk), .Q(s1));  // open: clr
  Register #(.width(32)) register_31 (.D(Write_Data), .en(x17_in), .clk(clk), .Q(x17));  // open: clr
  Demultiplexer #(.enable("false"), .select(5)) demultiplexer_1 (
    .out1(ra_in), .out2(sp_in), .out3(x3_in), .out4(x4_in), .out5(t0_in), .out6(t1_in), .out7(t2_in),
    .out8(s0_in), .out9(s1_in), .out10(a0_in), .out11(x11_in), .out12(x12_in), .out13(x13_in),
    .out14(x14_in), .out15(x15_in), .out16(x16_in), .out17(x17_in), .out18(x18_in), .out19(x19_in),
    .out20(x20_in), .out21(x21_in), .out22(x22_in), .out23(x23_in), .out24(x24_in), .out25(x25_in),
    .out26(x26_in), .out27(x27_in), .out28(x28_in), .out29(x29_in), .out30(x30_in), .out31(x31_in),
    .in(RegWEn), .sel(rd));  // open: out0

  // Other names for the same wires on the sheet: read_data1[31:0] = Read_Data_1; read_data2[31:0] = Read_Data_2;
  //   read_reg1[4:0] = rs1; read_reg2[4:0] = rs2; write_en = RegWEn; write_reg[4:0] = rd

  // Notes on the sheet:
  //   INPUTS to your circuit
  //   DON'T CHANGE THE LOCATIONS OF THE INPUTS AND OUTPUTS!
  //   These are DEBUG/TEST outputs from your circuit.
  //   OUTPUTS from your circuit
endmodule
