// Logisim project cpu-load,store_mem.circ as structural Verilog: 1 circuit, main circuit run_main
module run_main (
  output [31:0] ra,
  output [31:0] sp,
  output [31:0] t0,
  output [31:0] t1,
  output [31:0] t2,
  output [31:0] s0,
  output [31:0] s1,
  output [31:0] a0,
  output [31:0] Requested_Address,
  output [31:0] Requested_Instruction,
  output [15:0] Time_Step,
  output halt
);

  wire clk;

  Clock clock_1 (.out(clk));
  // Probe on Requested_Address
  // test_harness test_harness_1: pin names not known; wires that end beside it: Requested_Instruction, clk, Requested_Address, ra, sp, t0, t1, t2, s0, s1, a0
  ROM #(.addrWidth(14), .dataWidth(32)) rom_1 (.addr(Requested_Address[15:2]), .data(Requested_Instruction));
  // Probe on Requested_Instruction
  Counter #(.max('hffff), .width(16)) counter_1 (.clk(clk), .Q(Time_Step));  // open: clr, load, up, count, D, carry
  Comparator #(.width(16)) comparator_1 (.a(Time_Step), .b(16'h3a), .eq(halt));  // open: gt, lt

  // Other names for the same wires on the sheet: fetch_addr[31:0] = Requested_Address;
  //   Instruction[31:0] = Requested_Instruction

  // Notes on the sheet:
  //   contents of rom_1 (hex, n*v repeats v):
  //   FEF40413 01C48493 00350513 FF410113 00812023 00912223 00A12423 00010403 00110403 00210403 00310403
  //   00410403 00510403 00610403 00710403 00810403 00910403 00A10403 00B10403 00011483 00111483 00211483
  //   00411483 00511483 00611483 00811483 00911483 00A11483 00012503 00412503 00812503 00810023 008100A3
  //   00810123 008101A3 00810223 008102A3 00810323 008103A3 00810423 008104A3 00810523 008105A3 00911023
  //   009110A3 00911123 00911223 009112A3 00911323 00911423 009114A3 00911523 00A12023 00A12223 00A12423
  //   00C10113
  //   Instruction Memory
  //   Halts Execution After Constant # of Clock Cycles
  //   Constant
endmodule
