// Logisim project cpu-load,store_mem_alt.circ as structural Verilog: 1 circuit, main circuit run_main
module run_main (
  output [31:0] ra,
  output [31:0] sp,
  output [31:0] t0,
  output [31:0] t1,
  output [31:0] t2,
  output [31:0] s0,
  output [31:0] s1,
  output [31:0] a0,
  output [31:0] Requested_Address,
  output [31:0] Requested_Instruction,
  output [15:0] Time_Step,
  output halt
);

  wire clk;

  Clock clock_1 (.out(clk));
  // Probe on Requested_Address
  // test_harness test_harness_1: pin names not known; wires that end beside it: Requested_Instruction, clk, Requested_Address, ra, sp, t0, t1, t2, s0, s1, a0
  ROM #(.addrWidth(14), .dataWidth(32)) rom_1 (.addr(Requested_Address[15:2]), .data(Requested_Instruction));
  // Probe on Requested_Instruction
  Counter #(.max('hffff), .width(16)) counter_1 (.clk(clk), .Q(Time_Step));  // open: clr, load, up, count, D, carry
  Comparator #(.width(16)) comparator_1 (.a(Time_Step), .b(16'h3a), .eq(halt));  // open: gt, lt

  // Other names for the same wires on the sheet: fetch_addr[31:0] = Requested_Address;
  //   Instruction[31:0] = Requested_Instruction

  // Notes on the sheet:
  //   contents of rom_1 (hex, n*v repeats v):
  //   FEF40413 01C48493 00350513 FF410113 00812023 00912223 00A12423 00C10293 FFF28403 FFE28403 FFD28403
  //   FFC28403 FFB28403 FFA28403 FF928403 FF828403 FF728403 FF628403 FF528403 FF428403 FFE29483 FFD29483
  //   FFC29483 FFA29483 FF929483 FF829483 FF629483 FF529483 FF429483 FFC2A503 FF82A503 FF42A503 FE828FA3
  //   FE828F23 FE828EA3 FE828E23 FE828DA3 FE828D23 FE828CA3 FE828C23 FE828BA3 FE828B23 FE828AA3 FE828A23
  //   FE929F23 FE929EA3 FE929E23 FE929D23 FE929CA3 FE929C23 FE929B23 FE929AA3 FE929A23 FEA2AE23 FEA2AC23
  //   FEA2AA23
  //   Instruction Memory
  //   Halts Execution After Constant # of Clock Cycles
  //   Constant
endmodule
