// Logisim project cpu-load,store_mem_neg.circ as structural Verilog: 1 circuit, main circuit run_main
module run_main (
  output [31:0] ra,
  output [31:0] sp,
  output [31:0] t0,
  output [31:0] t1,
  output [31:0] t2,
  output [31:0] s0,
  output [31:0] s1,
  output [31:0] a0,
  output [31:0] Requested_Address,
  output [31:0] Requested_Instruction,
  output [15:0] Time_Step,
  output halt
);

  wire clk;

  Clock clock_1 (.out(clk));
  // Probe on Requested_Address
  // test_harness test_harness_1: pin names not known; wires that end beside it: Requested_Instruction, clk, Requested_Address, ra, sp, t0, t1, t2, s0, s1, a0
  ROM #(.addrWidth(14), .dataWidth(32)) rom_1 (.addr(Requested_Address[15:2]), .data(Requested_Instruction));
  // Probe on Requested_Instruction
  Counter #(.max('hffff), .width(16)) counter_1 (.clk(clk), .Q(Time_Step));  // open: clr, load, up, count, D, carry
  Comparator #(.width(16)) comparator_1 (.a(Time_Step), .b(16'h3a), .eq(halt));  // open: gt, lt

  // Other names for the same wires on the sheet: fetch_addr[31:0] = Requested_Address;
  //   Instruction[31:0] = Requested_Instruction

  // Notes on the sheet:
  //   contents of rom_1 (hex, n*v repeats v):
  //   FEF40413 01C48493 00350513 FF410113 00812023 00912223 00A12423 00C10113 FFF10403 FFE10403 FFD10403
  //   FFC10403 FFB10403 FFA10403 FF910403 FF810403 FF710403 FF610403 FF510403 FF410403 FFE11483 FFD11483
  //   FFC11483 FFA11483 FF911483 FF811483 FF611483 FF511483 FF411483 FFC12503 FF812503 FF412503 FE810FA3
  //   FE810F23 FE810EA3 FE810E23 FE810DA3 FE810D23 FE810CA3 FE810C23 FE810BA3 FE810B23 FE810AA3 FE810A23
  //   FE911F23 FE911EA3 FE911E23 FE911D23 FE911CA3 FE911C23 FE911B23 FE911AA3 FE911A23 FEA12E23 FEA12C23
  //   FEA12A23
  //   Instruction Memory
  //   Halts Execution After Constant # of Clock Cycles
  //   Constant
endmodule
